// Logisim project TP4.circ as structural Verilog: 1 circuit, main circuit main
module main (
  input  B3,
  input  B4,
  input  B5,
  input  B6,
  input  B7
);

  wire and_1_out, and_2_out, and_3_out, and_4_out, and_5_out, and_6_out, and_7_out, and_8_out, and_9_out,
       and_10_out, and_11_out, and_12_out, and_13_out, and_14_out, and_15_out, and_16_out, and_17_out,
       and_18_out, and_19_out, and_20_out, and_21_out, and_22_out, and_23_out, and_24_out, and_25_out,
       and_26_out, and_27_out, and_28_out, and_29_out, button_1_out, button_2_out, button_3_out,
       button_4_out, button_5_out, button_6_out, clock_1_out, nand_1_out, not_1_out, or_1_out, or_2_out,
       or_3_out, or_4_out, or_5_out, or_6_out, or_7_out, or_8_out, or_9_out, xor_1_out, xor_2_out, xor_3_out,
       xor_4_out, xor_5_out, xor_6_out, xor_7_out, xor_8_out, xor_9_out, xor_10_out, xor_11_out, xor_12_out,
       xor_13_out, xor_14_out, xor_15_out, xor_16_out, xor_17_out, xor_18_out, xor_19_out, xor_20_out,
       xor_21_out, xor_22_out, xor_23_out, xor_24_out, xor_25_out;
  wire [7:0] ACUMULADOR_q, MAR_q, MDR_q, multiplexer_1_out, multiplexer_2_out, multiplexer_3_out, or_10_out,
       PC_q, ram_1_dout;

  Button button_1 (.out(button_1_out));
  Button button_2 (.out(button_2_out));
  Button button_3 (.out(button_3_out));
  Button button_4 (.out(button_4_out));
  xor xor_1 (xor_1_out, button_4_out, button_1_out);
  xor xor_2 (xor_2_out, button_2_out, button_1_out);
  xor xor_3 (xor_3_out, button_3_out, button_1_out);
  xor xor_4 (xor_4_out, B3, button_1_out);
  xor xor_5 (xor_5_out, B4, button_1_out);
  xor xor_6 (xor_6_out, B5, button_1_out);
  xor xor_7 (xor_7_out, B6, button_1_out);
  xor xor_8 (xor_8_out, B7, button_1_out);
  xor xor_9 (xor_9_out, ACUMULADOR_q[0], xor_1_out);
  and and_1 (and_1_out, ACUMULADOR_q[0], xor_1_out);
  xor xor_10 (xor_10_out, ACUMULADOR_q[0], xor_2_out);
  and and_2 (and_2_out, ACUMULADOR_q[0], xor_2_out);
  xor xor_11 (xor_11_out, ACUMULADOR_q[0], xor_3_out);
  and and_3 (and_3_out, ACUMULADOR_q[0], xor_3_out);
  xor xor_12 (xor_12_out, ACUMULADOR_q[0], xor_4_out);
  and and_4 (and_4_out, ACUMULADOR_q[0], xor_4_out);
  xor xor_13 (xor_13_out, ACUMULADOR_q[0], xor_5_out);
  and and_5 (and_5_out, ACUMULADOR_q[0], xor_5_out);
  xor xor_14 (xor_14_out, ACUMULADOR_q[0], xor_6_out);
  and and_6 (and_6_out, ACUMULADOR_q[0], xor_6_out);
  xor xor_15 (xor_15_out, ACUMULADOR_q[0], xor_7_out);
  and and_7 (and_7_out, ACUMULADOR_q[0], xor_7_out);
  xor xor_16 (xor_16_out, ACUMULADOR_q[0], xor_8_out);
  and and_8 (and_8_out, ACUMULADOR_q[0], xor_8_out);
  xor xor_17 (xor_17_out, xor_9_out, button_1_out);
  and and_9 (and_9_out, xor_9_out, button_1_out);
  xor xor_18 (xor_18_out, xor_10_out, or_1_out);
  and and_10 (and_10_out, xor_10_out, or_1_out);
  xor xor_19 (xor_19_out, xor_11_out, or_2_out);
  and and_11 (and_11_out, xor_11_out, or_2_out);
  xor xor_20 (xor_20_out, xor_12_out, or_3_out);
  and and_12 (and_12_out, xor_12_out, or_3_out);
  and and_13 (and_13_out, xor_13_out, or_4_out);
  xor xor_21 (xor_21_out, xor_14_out, or_8_out);
  and and_14 (and_14_out, xor_14_out, or_8_out);
  xor xor_22 (xor_22_out, xor_16_out, or_9_out);
  and and_15 (and_15_out, xor_16_out, or_9_out);
  xor xor_23 (xor_23_out, xor_13_out, or_4_out);
  xor xor_24 (xor_24_out, xor_15_out, or_5_out);
  and and_16 (and_16_out, xor_15_out, or_5_out);
  or or_1 (or_1_out, and_9_out, and_1_out);
  or or_2 (or_2_out, and_10_out, and_2_out);
  or or_3 (or_3_out, and_11_out, and_3_out);
  or or_4 (or_4_out, and_12_out, and_4_out);
  or or_5 (or_5_out, and_14_out, and_6_out);
  or or_6 (or_6_out, and_15_out, and_8_out);
  xor xor_25 (xor_25_out, ACUMULADOR_q[0], button_4_out);
  nand nand_1 (nand_1_out, ACUMULADOR_q[0], button_4_out);
  and and_17 (and_17_out, ACUMULADOR_q[0], button_4_out);
  or or_7 (or_7_out, ACUMULADOR_q[0], button_4_out);
  or or_8 (or_8_out, and_13_out, and_5_out);
  or or_9 (or_9_out, and_16_out, and_7_out);
  Button button_5 (.out(button_5_out));
  Button button_6 (.out(button_6_out));
  not not_1 (not_1_out, button_6_out);
  and and_18 (and_18_out, not_1_out, button_5_out, xor_17_out);
  and and_19 (and_19_out, not_1_out, button_5_out, xor_18_out);
  and and_20 (and_20_out, not_1_out, button_5_out, xor_19_out);
  and and_21 (and_21_out, not_1_out, button_5_out, xor_20_out);
  and and_22 (and_22_out, not_1_out, button_5_out, xor_23_out);
  and and_23 (and_23_out, not_1_out, button_5_out, xor_21_out);
  and and_24 (and_24_out, not_1_out, button_5_out, xor_24_out);
  and and_25 (and_25_out, not_1_out, button_5_out, xor_22_out);
  and and_26 (and_26_out, not_1_out, button_5_out, or_7_out);
  and and_27 (and_27_out, not_1_out, button_5_out, xor_25_out);
  and and_28 (and_28_out, not_1_out, button_5_out, nand_1_out);
  and and_29 (and_29_out, not_1_out, button_5_out, and_17_out);
  Register ACUMULADOR (.D(or_10_out), .clk(clock_1_out), .Q(ACUMULADOR_q));  // open: en, clr
  or or_10 (or_10_out[0], and_18_out, and_19_out, and_20_out, and_21_out, and_22_out, and_23_out, and_24_out, and_25_out, and_26_out, and_27_out, and_28_out, and_29_out);
  Clock clock_1 (.out(clock_1_out));
  Multiplexer #(.select(2), .width(2)) multiplexer_1 (
    .in0(MAR_q[1:0]), .in3(MDR_q[1:0]), .out(multiplexer_1_out[1:0]));  // open: in1, in2, sel
  RAM ram_1 (.addr(multiplexer_1_out), .dout(ram_1_dout));  // open: we, oe, clk, din
  Register PC (.clk(clock_1_out), .Q(PC_q));  // open: D, en, clr
  Register IR (.D(ram_1_dout), .clk(clock_1_out));  // open: en, Q, clr
  Multiplexer #(.select(2), .width(2)) multiplexer_2 (
    .in1(ram_1_dout[1:0]), .in3(PC_q[1:0]), .out(multiplexer_2_out[1:0]));  // open: in0, in2, sel
  Register MAR (.D(multiplexer_2_out), .clk(clock_1_out), .Q(MAR_q));  // open: en, clr
  Multiplexer #(.select(2), .width(2)) multiplexer_3 (
    .in1(ram_1_dout[1:0]), .in3(ACUMULADOR_q[1:0]), .out(multiplexer_3_out[1:0]));  // open: in0, in2, sel
  Register MDR (.D(multiplexer_3_out), .clk(clock_1_out), .Q(MDR_q));  // open: en, clr
  // Pins of 1 and 8 bits meet at or_10_out
  // Pins of 1 and 2 and 8 bits meet at ACUMULADOR_q
  // Pins of 2 and 8 bits meet at MAR_q
  // Pins of 2 and 8 bits meet at MDR_q
  // Pins of 2 and 8 bits meet at multiplexer_1_out
  // Pins of 2 and 8 bits meet at ram_1_dout
  // Pins of 2 and 8 bits meet at PC_q
  // Pins of 2 and 8 bits meet at multiplexer_2_out
  // Pins of 2 and 8 bits meet at multiplexer_3_out

  // Notes on the sheet:
  //   A0
  //   B0
  //   Cin
  //   B1
  //   B2
  //   A1
  //   A2
  //   A3
  //   A4
  //   A5
  //   A6
  //   A7
  //   S0
  //   S1
endmodule
