// Logisim project TP5_Dominguez.circ as structural Verilog: 1 circuit, main circuit main
module main (
  input  [7:0] B
);

  wire clock_1_out, clock_2_out;
  wire [7:0] A_q, adder_1_out, and_1_out, IR_HIGH_q, multiplexer_1_out, nand_1_out, or_1_out, PC_q,
       rom_1_data, subtractor_1_out, xor_1_out;
  wire [15:0] IR_q, MDR_q, ram_1_dout;

  Register PC (.en(rom_1_data[6]), .Q(PC_q));  // open: D, clk, clr
  Register MAR (.en(rom_1_data[1]), .Q(PC_q));  // open: D, clk, clr
  Clock clock_1 (.out(clock_1_out));
  RAM #(.dataWidth(16)) ram_1 (
    .addr(PC_q), .we(rom_1_data[7]), .oe(rom_1_data[2]), .clk(clock_1_out), .dout(ram_1_dout));  // open: din
  Clock clock_2 (.out(clock_2_out));
  Register #(.width(16)) MDR (.D(ram_1_dout), .en(rom_1_data[3]), .clk(clock_2_out), .Q(MDR_q));  // open: clr
  Register #(.width(16)) IR (.D(MDR_q), .clk(clock_2_out), .Q(IR_q));  // open: en, clr
  Subtractor subtractor_1 (.a(A_q), .b(B), .out(subtractor_1_out));  // open: bin, bout
  Adder adder_1 (.a(A_q), .b(B), .out(adder_1_out));  // open: cin, cout
  assign and_1_out = A_q & B;  // AND_Gate and_1, 8 bits wide
  assign or_1_out = A_q | B;  // OR_Gate or_1, 8 bits wide
  assign nand_1_out = ~(A_q & B);  // NAND_Gate nand_1, 8 bits wide
  assign xor_1_out = A_q ^ B;  // XOR_Gate xor_1, 8 bits wide
  Register IR_LOW (.D(IR_q[7:0]), .clk(clock_2_out), .Q(B));  // open: en, clr
  Register IR_HIGH (.D(IR_q[15:8]), .clk(clock_2_out), .Q(IR_HIGH_q));  // open: en, clr
  Multiplexer #(.select(4), .width(8)) multiplexer_1 (
    .in4(subtractor_1_out), .in5(adder_1_out), .in6(and_1_out), .in7(or_1_out), .in8(nand_1_out),
    .in9(xor_1_out), .out(multiplexer_1_out));  // open: in0, in1, in2, in3, in10, in11, in12, in13, in14, in15, sel
  Register A (.D(multiplexer_1_out), .en(rom_1_data[0]), .Q(A_q), .clr(rom_1_data[4]));  // open: clk
  ROM rom_1 (.addr(IR_HIGH_q), .data(rom_1_data));

  // Notes on the sheet:
  //   ALU
endmodule
