// Logisim project TP5_Dominguez_2.circ as structural Verilog: 1 circuit, main circuit main
module main (
);

  wire clock_1_out, clock_3_out;
  wire [2:1] undriven_2;
  wire [7:0] A_q, adder_1_out, and_1_out, B_q, IR_LOW_q, MAR_q, multiplexer_1_out, multiplexer_2_out,
       multiplexer_3_out, nand_1_out, or_1_out, PC_q, ram_1_dout, rom_1_data, rom_2_data, subtractor_1_out,
       undriven, xor_1_out;

  Multiplexer multiplexer_1 (.in0(undriven[0]), .in1(MAR_q[0]), .out(multiplexer_1_out[0]), .sel(rom_2_data[5]));
  Register PC (.D(multiplexer_1_out), .clk(clock_1_out), .Q(PC_q));  // open: en, clr
  Register MAR (.D(IR_LOW_q), .en(rom_2_data[6]), .clk(clock_1_out), .Q(MAR_q));  // open: clr
  Clock clock_1 (.out(clock_1_out));
  RAM ram_1 (.addr(undriven), .we(rom_2_data[7]), .clk(clock_1_out), .dout(ram_1_dout));  // open: oe, din
  ROM rom_1 (.addr(PC_q), .data(rom_1_data));
  Clock clock_2 (.out(rom_2_data[2]));
  Multiplexer multiplexer_2 (.in0(A_q[0]), .in1(ram_1_dout[0]), .out(multiplexer_2_out[0]));  // open: sel
  Register B (.D(ram_1_dout), .en(rom_2_data[2]), .clk(rom_2_data[2]), .Q(B_q));  // open: clr
  Register IR_LOW (.D(rom_1_data), .en(rom_2_data[3]), .clk(clock_3_out), .Q(IR_LOW_q));  // open: clr
  Register IR_HIGH (.D(rom_1_data), .en(rom_2_data[4]), .clk(clock_3_out), .Q(IR_LOW_q));  // open: clr
  Clock clock_3 (.out(clock_3_out));
  Subtractor subtractor_1 (.a(multiplexer_2_out), .b(B_q), .out(subtractor_1_out));  // open: bin, bout
  Adder adder_1 (.a(multiplexer_2_out), .b(B_q), .out(adder_1_out));  // open: cin, cout
  assign and_1_out = multiplexer_2_out & B_q;  // AND_Gate and_1, 8 bits wide
  assign or_1_out = multiplexer_2_out | B_q;  // OR_Gate or_1, 8 bits wide
  assign nand_1_out = ~(multiplexer_2_out & B_q);  // NAND_Gate nand_1, 8 bits wide
  assign xor_1_out = multiplexer_2_out ^ B_q;  // XOR_Gate xor_1, 8 bits wide
  ROM rom_2 (.addr(IR_LOW_q), .data(rom_2_data));
  Multiplexer #(.select(3), .width(8)) multiplexer_3 (
    .in1(subtractor_1_out), .in2(adder_1_out), .in3(and_1_out), .in4(or_1_out), .in5(nand_1_out),
    .in6(xor_1_out), .out(multiplexer_3_out), .sel({undriven_2, rom_2_data[0]}));  // open: in0, in7
  Register A (.D(multiplexer_3_out), .en(rom_2_data[1]), .clk(rom_2_data[2]), .Q(A_q));  // open: clr
  // Pins of 1 and 3 bits meet at {undriven_2, rom_2_data[0]}
  // Pins of 1 and 8 bits meet at multiplexer_2_out
  // Pins of 1 and 8 bits meet at A_q
  // Pins of 1 and 8 bits meet at ram_1_dout
  // Pins of 1 and 8 bits meet at undriven
  // Pins of 1 and 8 bits meet at MAR_q
  // Pins of 1 and 8 bits meet at multiplexer_1_out

  // Notes on the sheet:
  //   ALU
endmodule
