// Logisim project TP5_Dominguez_3.circ as structural Verilog: 2 circuits, main circuit main
module main (
);

  wire clock_1_out, clock_2_out, clock_3_out, clock_4_out, clock_5_out, clock_6_out, clock_7_out, undriven;
  wire [1:1] undriven_2;
  wire [7:0] A_q, adder_1_out, alu_1_out_4, B_q, IR_HIGH_q, IR_LOW_q, MAR_q, multiplexer_1_out, PC_q,
       ram_1_dout;
  wire [15:0] rom_1_data, rom_2_data;

  Adder adder_1 (.a(PC_q), .out(adder_1_out));  // open: b, cin, cout
  Register PC (.D(adder_1_out), .en(rom_2_data[13]), .clk(clock_1_out), .Q(PC_q));  // open: clr
  Clock clock_1 (.out(clock_1_out));
  ROM #(.dataWidth(16)) rom_1 (.addr(PC_q), .data(rom_1_data));
  Register IR_LOW (.D(rom_1_data[7:0]), .en(rom_2_data[2]), .clk(clock_2_out), .Q(IR_LOW_q));  // open: clr
  Clock clock_2 (.out(clock_2_out));
  Register IR_HIGH (.D(rom_1_data[15:8]), .en(undriven), .clk(clock_3_out), .Q(IR_HIGH_q));  // open: clr
  Clock clock_3 (.out(clock_3_out));
  Register MAR (.D(IR_LOW_q), .en(rom_2_data[10]), .clk(clock_4_out), .Q(MAR_q));  // open: clr
  Clock clock_4 (.out(clock_4_out));
  RAM ram_1 (.addr(MAR_q), .we(rom_2_data[3]), .oe(rom_2_data[4]), .clk(clock_5_out), .dout(ram_1_dout));  // open: din
  ROM #(.addrWidth(4), .dataWidth(16)) rom_2 (.addr(IR_HIGH_q[7:4]), .data(rom_2_data));
  Clock clock_5 (.out(clock_5_out));
  Multiplexer #(.width(8)) multiplexer_1 (.in0(ram_1_dout), .in1(A_q), .out(multiplexer_1_out));  // open: sel
  Register B (.D(ram_1_dout), .en(rom_2_data[5]), .clk(clock_6_out), .Q(B_q));  // open: clr
  Clock clock_6 (.out(clock_6_out));
  ALU alu_1 (.A(multiplexer_1_out), .B(B_q), .Cin({rom_2_data[1], undriven_2[1], rom_2_data[7]}), .out_4(alu_1_out_4));
  Register A (.D(alu_1_out_4), .en(rom_2_data[6]), .clk(clock_7_out), .Q(A_q));  // open: clr
  Clock clock_7 (.out(clock_7_out));

  // Notes on the sheet:
  //   contents of rom_2 (hex, n*v repeats v):
  //   0 1 10 11 100 101 110 111 1000 1001 1010 1011 1100 1101 1110 1111
endmodule

module ALU (
  input  [7:0] A,
  input  [7:0] B,
  input  [2:0] Cin,
  output [7:0] out_4
);

  wire adder_1_cout;
  wire [7:0] adder_1_out, and_1_out, nand_1_out, or_1_out, subtractor_1_out, xor_1_out;

  Adder adder_1 (.a(B), .b(A), .out(adder_1_out), .cout(adder_1_cout));  // open: cin
  Subtractor subtractor_1 (.b(A), .out(subtractor_1_out), .bin(adder_1_cout));  // open: a, bout
  assign and_1_out = B & A;  // AND_Gate and_1, 8 bits wide
  assign or_1_out = B | A;  // OR_Gate or_1, 8 bits wide
  assign xor_1_out = B ^ A;  // XOR_Gate xor_1, 8 bits wide
  assign nand_1_out = ~(B & A);  // NAND_Gate nand_1, 8 bits wide
  Multiplexer #(.select(3), .width(8)) multiplexer_1 (
    .in2(adder_1_out), .in3(subtractor_1_out), .in4(and_1_out), .in5(or_1_out), .in6(xor_1_out),
    .in7(nand_1_out), .out(out_4), .sel(Cin));  // open: in0, in1
endmodule
