// Logisim project TP6.circ as structural Verilog: 2 circuits, main circuit main
// PC
module main (
  input  [7:0] in_1,
  input  [3:0] in_2,
  input  [2:0] in_3,
  output out_4
);

  wire bcd_to_7_segment_decoder_3_p1, binary_to_bcd_converter_1_p2, binary_to_bcd_converter_1_p4,
       clock_1_out, clock_2_out, clock_3_out, clock_4_out, DMX, IR_HIGH, IR_LOW, MAR, MEM, PC;
  wire [2:0] adder_2_out, register_2_q;
  wire [3:0] IR_HIGH_q;
  wire [7:0] A_q, adder_1_out, alu_1_s, B_q, demultiplexer_1_out0, demultiplexer_1_out1, IR_LOW_q, MAR_q,
       multiplexer_1_out, register_1_q, rom_1_data;
  wire [15:0] ram_1_dout, rom_2_data;

  Clock clock_1 (.out(clock_1_out));
  Register register_1 (.D(adder_1_out), .en(PC), .clk(clock_1_out), .Q(register_1_q));  // open: clr
  Adder adder_1 (.a(in_1), .b(register_1_q), .out(adder_1_out), .cout(out_4));  // open: cin
  ROM rom_1 (.addr(register_1_q), .data(rom_1_data));
  Clock clock_2 (.out(clock_2_out));
  Demultiplexer #(.width(8)) demultiplexer_1 (
    .out0(demultiplexer_1_out0), .out1(demultiplexer_1_out1), .in(rom_1_data), .sel(DMX));
  Register #(.width(3)) register_2 (
    .D(adder_2_out), .en(1'b1), .clk(clock_2_out), .Q(register_2_q), .clr(rom_2_data[13]));
  Register u_IR_LOW (.D(demultiplexer_1_out0), .en(IR_LOW), .clk(clock_3_out), .Q(IR_LOW_q));  // open: clr
  Register u_IR_HIGH (.D(demultiplexer_1_out1), .en(IR_HIGH), .clk(clock_3_out), .Q({in_2, IR_HIGH_q}));  // open: clr
  Clock clock_3 (.out(clock_3_out));
  Adder #(.width(3)) adder_2 (.a(in_3), .b(register_2_q), .out(adder_2_out));  // open: cin, cout
  Register u_MAR (.D(IR_LOW_q), .en(MAR), .clk(clock_3_out), .Q(MAR_q));  // open: clr
  ROM #(.addrWidth(7), .dataWidth(16)) rom_2 (
    .addr({adder_2_out, in_2}),
    .data({rom_2_data[15:10], PC, DMX, IR_LOW, IR_HIGH, rom_2_data[5], MAR, MEM, rom_2_data[2:0]}));
  RAM #(.dataWidth(16)) ram_1 (
    .addr(MAR_q), .we(rom_2_data[2]), .oe(MEM), .clk(clock_3_out), .dout(ram_1_dout));  // open: din
  Register B (.D(ram_1_dout[15:8]), .en(rom_2_data[1]), .clk(clock_4_out), .Q(B_q));  // open: clr
  Clock clock_4 (.out(clock_4_out));
  Multiplexer #(.width(8)) multiplexer_1 (
    .in0(A_q), .in1(ram_1_dout[7:0]), .out(multiplexer_1_out), .sel(rom_2_data[5]));
  ALU alu_1 (.A(multiplexer_1_out), .B(B_q), .Cin(rom_2_data[12:10]), .S(alu_1_s));
  Register A (.D(alu_1_s), .en(rom_2_data[0]), .clk(clock_4_out), .Q(A_q));  // open: clr
  // BCD_to_7_Segment_decoder bcd_to_7_segment_decoder_1: pin names not known
  // Binary_to_BCD_converter #(.binvalue(8)) binary_to_bcd_converter_1: pin names not known; wires that end beside it: alu_1_s, binary_to_bcd_converter_1_p2, binary_to_bcd_converter_1_p2, binary_to_bcd_converter_1_p4, binary_to_bcd_converter_1_p4
  // BCD_to_7_Segment_decoder bcd_to_7_segment_decoder_2: pin names not known
  // BCD_to_7_Segment_decoder bcd_to_7_segment_decoder_3: pin names not known; wires that end beside it: bcd_to_7_segment_decoder_3_p1, bcd_to_7_segment_decoder_3_p1

  // Notes on the sheet:
  //   contents of rom_1 (hex, n*v repeats v):
  //   16 22 3 0 74
  //   contents of rom_2 (hex, n*v repeats v):
  //   6666 15*0 78
endmodule

module ALU (
  input  [7:0] A,
  input  [7:0] B,
  input  [2:0] Cin,
  output [7:0] S
);

  wire adder_1_cout;
  wire [7:0] adder_1_out, and_1_out, nand_1_out, or_1_out, subtractor_1_out, xor_1_out;

  Adder adder_1 (.a(A), .b(B), .out(adder_1_out), .cout(adder_1_cout));  // open: cin
  Subtractor subtractor_1 (.a(A), .b(B), .out(subtractor_1_out), .bin(adder_1_cout));  // open: bout
  assign and_1_out = A & B;  // AND_Gate and_1, 8 bits wide
  assign or_1_out = A | B;  // OR_Gate or_1, 8 bits wide
  assign nand_1_out = ~(A & B);  // NAND_Gate nand_1, 8 bits wide
  assign xor_1_out = A ^ B;  // XOR_Gate xor_1, 8 bits wide
  Multiplexer #(.select(3), .width(8)) multiplexer_1 (
    .in0(adder_1_out), .in1(subtractor_1_out), .in2(and_1_out), .in3(or_1_out), .in4(nand_1_out),
    .in5(xor_1_out), .out(S), .sel(Cin));  // open: in6, in7
endmodule
