// Logisim project orga.circ as structural Verilog: 1 circuit, main circuit main
module main (
);

  wire and_1_out, and_2_out, and_3_out, and_4_out, and_5_out, and_6_out, and_7_out, and_8_out, and_9_out,
       and_10_out, and_11_out, and_12_out, and_13_out, and_14_out, and_15_out, and_16_out, and_17_out,
       and_18_out, and_19_out, and_20_out, and_21_out, and_22_out, and_23_out, and_24_out, and_25_out,
       and_26_out, and_27_out, and_28_out, and_29_out, buffer_1_out, nand_1_out, or_1_out, or_2_out,
       or_3_out, or_4_out, or_5_out, or_6_out, or_7_out, or_8_out, or_9_out, undriven, undriven_2, xor_1_out,
       xor_2_out, xor_3_out, xor_4_out, xor_5_out, xor_6_out, xor_7_out, xor_8_out, xor_9_out, xor_10_out,
       xor_11_out, xor_12_out, xor_13_out, xor_14_out, xor_15_out, xor_16_out, xor_17_out, xor_18_out,
       xor_19_out, xor_20_out, xor_21_out, xor_22_out, xor_23_out, xor_24_out, xor_25_out;
  wire [0:0] or_10_out;

  xor xor_1 (xor_1_out, 1'b1, 1'b1);
  xor xor_2 (xor_2_out, 1'b1, 1'b1);
  xor xor_3 (xor_3_out, 1'b1, 1'b1);
  xor xor_4 (xor_4_out, 1'b1, 1'b1);
  xor xor_5 (xor_5_out, 1'b1, 1'b1);
  xor xor_6 (xor_6_out, 1'b1, 1'b1);
  xor xor_7 (xor_7_out, 1'b1, xor_1_out);
  and and_1 (and_1_out, 1'b1, xor_1_out);
  xor xor_8 (xor_8_out, 1'b1, xor_2_out);
  and and_2 (and_2_out, 1'b1, xor_2_out);
  xor xor_9 (xor_9_out, 1'b1, xor_3_out);
  and and_3 (and_3_out, 1'b1, xor_3_out);
  xor xor_10 (xor_10_out, 1'b1, xor_4_out);
  and and_4 (and_4_out, 1'b1, xor_4_out);
  xor xor_11 (xor_11_out, 1'b1, 1'b1);
  xor xor_12 (xor_12_out, 1'b1, 1'b1);
  xor xor_13 (xor_13_out, 1'b1, xor_5_out);
  and and_5 (and_5_out, 1'b1, xor_5_out);
  xor xor_14 (xor_14_out, 1'b1, xor_6_out);
  and and_6 (and_6_out, 1'b1, xor_6_out);
  xor xor_15 (xor_15_out, 1'b1, xor_11_out);
  and and_7 (and_7_out, 1'b1, xor_11_out);
  xor xor_16 (xor_16_out, 1'b1, xor_12_out);
  and and_8 (and_8_out, 1'b1, xor_12_out);
  xor xor_17 (xor_17_out, xor_7_out, 1'b1);
  buf and_9 (and_9_out, xor_7_out);  // AND_Gate
  xor xor_18 (xor_18_out, xor_8_out, or_1_out);
  and and_10 (and_10_out, xor_8_out, or_1_out);
  xor xor_19 (xor_19_out, xor_9_out, or_2_out);
  and and_11 (and_11_out, xor_9_out, or_2_out);
  xor xor_20 (xor_20_out, xor_10_out, or_3_out);
  and and_12 (and_12_out, xor_10_out, or_3_out);
  xor xor_21 (xor_21_out, xor_13_out, or_4_out);
  and and_13 (and_13_out, xor_13_out, or_4_out);
  xor xor_22 (xor_22_out, xor_14_out, or_5_out);
  and and_14 (and_14_out, xor_14_out, or_5_out);
  xor xor_23 (xor_23_out, xor_15_out, or_6_out);
  and and_15 (and_15_out, xor_15_out, or_6_out);
  xor xor_24 (xor_24_out, xor_16_out, or_7_out);
  and and_16 (and_16_out, xor_16_out, or_7_out);
  or or_1 (or_1_out, and_9_out, and_1_out);
  or or_2 (or_2_out, and_10_out, and_2_out);
  or or_3 (or_3_out, and_11_out, and_3_out);
  or or_4 (or_4_out, and_12_out, and_4_out);
  or or_5 (or_5_out, and_13_out, and_5_out);
  or or_6 (or_6_out, and_14_out, and_6_out);
  or or_7 (or_7_out, and_15_out, and_7_out);
  or or_8 (or_8_out, and_16_out, and_8_out);
  xor xor_25 (xor_25_out, 1'b1, 1'b1);
  nand nand_1 (nand_1_out, 1'b1, 1'b1);
  and and_17 (and_17_out, 1'b1, 1'b1);
  or or_9 (or_9_out, 1'b1, 1'b1);
  buf buffer_1 (buffer_1_out, undriven_2);
  and and_18 (and_18_out, buffer_1_out, undriven, xor_17_out);
  and and_19 (and_19_out, buffer_1_out, undriven, xor_18_out);
  and and_20 (and_20_out, buffer_1_out, undriven, xor_19_out);
  and and_21 (and_21_out, buffer_1_out, undriven, xor_20_out);
  and and_22 (and_22_out, buffer_1_out, undriven, xor_21_out);
  and and_23 (and_23_out, buffer_1_out, undriven, xor_22_out);
  and and_24 (and_24_out, buffer_1_out, undriven, xor_23_out);
  and and_25 (and_25_out, buffer_1_out, undriven, xor_24_out);
  and and_26 (and_26_out, buffer_1_out, undriven, xor_25_out);
  and and_27 (and_27_out, buffer_1_out, undriven, nand_1_out);
  and and_28 (and_28_out, buffer_1_out, undriven, and_17_out);
  and and_29 (and_29_out, buffer_1_out, undriven, or_9_out);
  or or_10 (or_10_out[0], and_18_out, and_19_out, and_20_out, and_21_out, and_22_out, and_23_out, and_24_out, and_25_out, and_26_out, and_27_out, and_28_out, and_29_out);
  // Pins of 1 and 8 bits meet at {8{1'b1}}
  // Pins of 1 and 8 bits meet at {8{1'b1}}
  // Pins of 1 and 8 bits meet at {8{1'b1}}
  // Pins of 1 and 8 bits meet at {8{1'b1}}
  // Pins of 1 and 8 bits meet at {8{1'b1}}
  // Pins of 1 and 8 bits meet at {8{1'b1}}
  // Pins of 1 and 8 bits meet at {8{1'b1}}
  // Pins of 1 and 8 bits meet at {8{1'b1}}
  // Pins of 1 and 8 bits meet at {8{1'b1}}
  // Pins of 1 and 8 bits meet at {8{1'b1}}
  // Pins of 1 and 8 bits meet at {8{1'b1}}
  // Pins of 1 and 8 bits meet at {8{1'b1}}
endmodule
